// Logisim project Busca_Instrucao.circ as structural Verilog
module \Busca_Instrução  (
  input  Enable,
  input  Clock,
  input  Clear,
  output [7:0] PC
);

  wire [7:0] adder_1_out;

  Register u_PC (.D(adder_1_out), .en(Enable), .Q(PC), .clk(Clock), .clr(Clear));
  Adder adder_1 (.a(8'h1), .b(PC), .out(adder_1_out));  // open: cin, cout
endmodule
