// Logisim project MIPS8bits.circ as structural Verilog: 3 circuits, main circuit Mini-Mips-8bits
module Mini_Mips_8bits (
  input  IncPc,
  input  Clear,
  input  EscReg,
  input  ClearReg,
  input  RegDst,
  input  UlaFonte,
  input  [2:0] ControleULA,
  input  EscMem,
  input  ClearData,
  input  MemParaReg,
  output [3:0] OPCODE,
  output [7:0] SaidaULA,
  output [7:0] Entrada_B_Reg,
  output [7:0] Op1,
  output out_15,
  output [7:0] Op2,
  output [7:0] \Endereço ,
  output [7:0] Data,
  output [15:0] \Instrução 
);

  wire clk, not_1_out;
  wire [2:0] multiplexer_1_out;
  wire [7:0] ram_1_data;

  Clock u_Clk (.out(clk));
  \Busca_Instrução  \busca_instrução_1  (.Enable(IncPc), .Clock(clk), .Clear(Clear), .PC(\Endereço ));
  Hex_Digit_Display hex_digit_display_1 (.value(\Endereço [7:4]), .dp(1'b1));
  Hex_Digit_Display hex_digit_display_2 (.value(\Endereço [3:0]), .dp(1'b1));
  ROM #(.dataWidth(16)) rom_1 (.addr(\Endereço ), .data(\Instrução ));  // open: sel
  Banco_registradores_Mini_Mips8Bits_sMux banco_registradores_mini_mips8bits_smux_1 (
    .Read_Register_1(\Instrução [11:9]), .Read_Register_2(\Instrução [8:6]), .Write_data(Entrada_B_Reg),
    .RegWrite(EscReg), .Write_Register(multiplexer_1_out), .Clock(clk), .Clear(ClearReg), .Read_data_1(Op1),
    .Read_data_2(Data));
  Multiplexer #(.width(3), .enable("false")) multiplexer_1 (
    .in0(\Instrução [8:6]), .in1(\Instrução [5:3]), .out(multiplexer_1_out), .sel(RegDst));
  Multiplexer #(.width(8), .enable("false")) multiplexer_2 (
    .in0(Data), .in1({{3{\Instrução [5]}}, \Instrução [4:0]}), .out(Op2), .sel(UlaFonte));
  ULA ula_1 (.Flag(out_15), .resultado(SaidaULA), .in_1(ControleULA), .in_2(Op1), .in_3(Op2));
  not not_1 (not_1_out, EscMem);
  RAM #(.bus("separate")) ram_1 (
    .addr(SaidaULA), .din(Data), .data(ram_1_data), .str(EscMem), .clk(clk), .ld(not_1_out), .clr(ClearData));  // open: sel
  Multiplexer #(.width(8), .enable("false")) multiplexer_3 (
    .in0(ram_1_data), .in1(SaidaULA), .out(Entrada_B_Reg), .sel(MemParaReg));

  assign OPCODE = \Instrução [15:12];

  // Notes on the sheet:
  //   Clear: pull=down
  //   MemParaReg: pull=up
  //   EscReg: pull=up
  //   UlaFonte: pull=up
  //   IncPc: pull=down
  //   OPCODE: pull=down
  //   ClearData: pull=down
  //   ControleULA: pull=up
  //   EscMem: pull=up
  //   RegDst: pull=up
  //   Endereço: pull=down
  //   ClearReg: pull=down
  //   Instrução: pull=down
  //   contents of rom_1 (hex, n*v repeats v):
  //   b08a b0cb 4041 20 8603 520 65a 2004 f10c
endmodule

// RegDst
module Mini_MIPS_8bits_Controle (
  input  ClearReg,
  input  Clear,
  input  ClearData,
  output [3:0] OPCODE,
  output [7:0] SaidaULA,
  output [7:0] Entrada_B_Reg,
  output [7:0] Op1,
  output out_8,
  output [7:0] Op2,
  output [7:0] \Endereço ,
  output [7:0] Data,
  output [15:0] \Instrução ,
  output [2:0] ControleUla,
  output RegDst,
  output EscMem,
  output MemParaReg,
  output UlaFonte
);

  wire clk, EscReg, IncPc, not_1_out;
  wire [2:0] multiplexer_1_out;
  wire [7:0] ram_1_data;

  Clock u_Clk (.out(clk));
  \Busca_Instrução  \busca_instrução_1  (.Enable(IncPc), .Clock(clk), .Clear(Clear), .PC(\Endereço ));
  Hex_Digit_Display hex_digit_display_1 (.value(\Endereço [7:4]), .dp(1'b1));
  Hex_Digit_Display hex_digit_display_2 (.value(\Endereço [3:0]), .dp(1'b1));
  // ControleMiniMips controleminimips_1: pin names not known; wires that end beside it: ControleUla[0], ControleUla[1], ControleUla[2], EscMem, EscReg, MemParaReg, UlaFonte, RegDst, IncPc, \Instrução [12], \Instrução [13], \Instrução [14], \Instrução [15]
  ROM #(.dataWidth(16)) rom_1 (.addr(\Endereço ), .data(\Instrução ));  // open: sel
  Banco_registradores_Mini_Mips8Bits_sMux banco_registradores_mini_mips8bits_smux_1 (
    .Read_Register_1(\Instrução [11:9]), .Read_Register_2(\Instrução [8:6]), .Write_data(Entrada_B_Reg),
    .RegWrite(EscReg), .Write_Register(multiplexer_1_out), .Clock(clk), .Clear(ClearReg), .Read_data_1(Op1),
    .Read_data_2(Data));
  Multiplexer #(.width(3), .enable("false")) multiplexer_1 (
    .in0(\Instrução [8:6]), .in1(\Instrução [5:3]), .out(multiplexer_1_out), .sel(RegDst));
  Multiplexer #(.width(8), .enable("false")) multiplexer_2 (
    .in0(Data), .in1({{3{\Instrução [5]}}, \Instrução [4:0]}), .out(Op2), .sel(UlaFonte));
  ULA ula_1 (.Flag(out_8), .resultado(SaidaULA), .in_1(ControleUla), .in_2(Op1), .in_3(Op2));
  not not_1 (not_1_out, EscMem);
  RAM #(.bus("separate")) ram_1 (
    .addr(SaidaULA), .din(Data), .data(ram_1_data), .str(EscMem), .clk(clk), .ld(not_1_out), .clr(ClearData));  // open: sel
  Multiplexer #(.width(8), .enable("false")) multiplexer_3 (
    .in0(ram_1_data), .in1(SaidaULA), .out(Entrada_B_Reg), .sel(MemParaReg));

  assign OPCODE = \Instrução [15:12];

  // Other names for the same wires on the sheet: Funct[2:0] = \Instrução [2:0]

  // Notes on the sheet:
  //   ClearReg: pull=down
  //   UlaFonte: pull=down
  //   OPCODE: pull=down
  //   ClearData: pull=down
  //   MemParaReg: pull=down
  //   Clear: pull=down
  //   ControleUla: pull=down
  //   EscMem: pull=down
  //   Instrução: pull=down
  //   Endereço: pull=down
  //   RegDst: pull=down
  //   contents of rom_1 (hex, n*v repeats v):
  //   0 4085 4043 458 410a f080 f104 b044 8088 8141 868a 2001
endmodule

module Mini_MIPS_Controle_Jump_Branch (
  input  Clear,
  input  ClearReg,
  input  ClearData,
  output [3:0] OPCODE,
  output [7:0] SaidaULA,
  output [7:0] Entrada_B_Reg,
  output [7:0] Op1,
  output out_8,
  output [7:0] Op2,
  output [7:0] \Endereço ,
  output [7:0] Data,
  output [15:0] \Instrução ,
  output [2:0] ControleUla,
  output [7:0] PC_Branch,
  output [7:0] PC_Jump,
  output RegDst,
  output EscMem,
  output MemParaReg,
  output UlaFonte
);

  wire Branch, clk, controleminimips_1_p15, EscReg, IncPc, Jump, not_1_out;
  wire [2:0] multiplexer_3_out;
  wire [7:0] multiplexer_1_out, multiplexer_2_out, PC_1, ram_1_data;

  Clock u_Clk (.out(clk));
  Multiplexer #(.width(8), .enable("false")) multiplexer_1 (
    .in0(PC_1), .in1(PC_Branch), .out(multiplexer_1_out), .sel(Branch));
  Multiplexer #(.width(8), .enable("false")) multiplexer_2 (
    .in0(multiplexer_1_out), .in1(\Instrução [7:0]), .out(multiplexer_2_out), .sel(Jump));
  Register PC (.D(multiplexer_2_out), .en(IncPc), .Q(\Endereço ), .clk(clk), .clr(Clear));
  Adder adder_1 (.a(8'h1), .b(\Endereço ), .out(PC_1));  // open: cin, cout
  // ControleMiniMips controleminimips_1: pin names not known; wires that end beside it: ControleUla[0], ControleUla[1], ControleUla[2], EscMem, EscReg, MemParaReg, UlaFonte, RegDst, IncPc, \Instrução [12], \Instrução [13], Jump, \Instrução [14], \Instrução [15], controleminimips_1_p15
  ROM #(.dataWidth(16)) rom_1 (.addr(\Endereço ), .data(\Instrução ));  // open: sel
  and and_1 (Branch, out_8, controleminimips_1_p15);
  Multiplexer #(.width(3), .enable("false")) multiplexer_3 (
    .in0(\Instrução [8:6]), .in1(\Instrução [5:3]), .out(multiplexer_3_out), .sel(RegDst));
  Banco_registradores_Mini_Mips8Bits_sMux banco_registradores_mini_mips8bits_smux_1 (
    .Read_Register_1(\Instrução [11:9]), .Read_Register_2(\Instrução [8:6]), .Write_data(Entrada_B_Reg),
    .RegWrite(EscReg), .Write_Register(multiplexer_3_out), .Clock(clk), .Clear(ClearReg), .Read_data_1(Op1),
    .Read_data_2(Data));
  Multiplexer #(.width(8), .enable("false")) multiplexer_4 (
    .in0(Data), .in1({{3{\Instrução [5]}}, \Instrução [4:0]}), .out(Op2), .sel(UlaFonte));
  ULA ula_1 (.Flag(out_8), .resultado(SaidaULA), .in_1(ControleUla), .in_2(Op1), .in_3(Op2));
  Adder adder_2 (.a({{3{\Instrução [5]}}, \Instrução [4:0]}), .b(PC_1), .out(PC_Branch));  // open: cin, cout
  RAM #(.bus("separate")) ram_1 (
    .addr(SaidaULA), .din(Data), .data(ram_1_data), .str(EscMem), .clk(clk), .ld(not_1_out), .clr(ClearData));  // open: sel
  not not_1 (not_1_out, EscMem);
  Multiplexer #(.width(8), .enable("false")) multiplexer_5 (
    .in0(ram_1_data), .in1(SaidaULA), .out(Entrada_B_Reg), .sel(MemParaReg));

  assign OPCODE = \Instrução [15:12];
  assign PC_Jump = \Instrução [7:0];

  // Other names for the same wires on the sheet: Funct[2:0] = \Instrução [2:0]; ZeroUla = out_8

  // Notes on the sheet:
  //   UlaFonte: pull=down
  //   Clear: pull=down
  //   ClearReg: pull=down
  //   ControleUla: pull=down
  //   MemParaReg: pull=down
  //   EscMem: pull=down
  //   OPCODE: pull=down
  //   ClearData: pull=down
  //   RegDst: pull=down
  //   Instrução: pull=down
  //   Endereço: pull=down
  //   contents of rom_1 (hex, n*v repeats v):
  //   4085 4043 458 410a f080 f104 b044 8088 8141 868a 2000
endmodule
