// Logisim project ULA.circ as structural Verilog: 4 circuits, main circuit ULA
module ULA (
  input  [2:0] in_1,
  input  [7:0] in_2,
  input  [7:0] in_3,
  output Flag,
  output [7:0] resultado
);

  wire and_1_out, and_3_out, comparator_1_eq, not_1_out, not_2_out, not_3_out, somador_subtrator_1_flag;
  wire [7:0] and_2_resultado, or_1_resultado, somador_subtrator_1_resultado;

  not not_1 (not_1_out, in_1[2]);
  not not_2 (not_2_out, in_1[0]);
  and and_1 (and_1_out, not_1_out, in_1[1], not_2_out);
  Somador_Subtrator somador_subtrator_1 (
    .in_1(and_1_out), .Operando_1(in_2), .Operando_2(in_3), .resultado(somador_subtrator_1_resultado),
    .Flag(somador_subtrator_1_flag));
  AND and_2 (.resultado(and_2_resultado), .in_1(in_2), .in_2(in_3));
  OR or_1 (.resultado(or_1_resultado), .in_1(in_2), .in_2(in_3));
  Comparator comparator_1 (.a(in_3), .b(in_2), .eq(comparator_1_eq));  // open: gt, lt
  not not_3 (not_3_out, in_1[0]);
  and and_3 (and_3_out, in_1[2], in_1[1], not_3_out);
  Multiplexer #(.disabled(0), .enable("false")) multiplexer_1 (
    .in0(somador_subtrator_1_flag), .in1(comparator_1_eq), .out(Flag), .sel(and_3_out));
  Multiplexer #(.select(3), .width(8), .enable("false")) multiplexer_2 (
    .in0(somador_subtrator_1_resultado), .in1(somador_subtrator_1_resultado),
    .in2(somador_subtrator_1_resultado), .in3(somador_subtrator_1_resultado), .in4(and_2_resultado),
    .in5(or_1_resultado), .in6({8{1'b0}}), .in7(somador_subtrator_1_resultado), .out(resultado), .sel(in_1));

  // Other names for the same wires on the sheet: operando_1[7:0] = in_2; operando_2[7:0] = in_3; UlaOp[2:0] = in_1

  // Notes on the sheet:
  //   in_3: pull=down
  //   Flag: pull=down
  //   in_1: pull=down
  //   in_2: pull=down
  //    000 -> ADD  [0]
  //   001 -> ADDi [1]   
  //    010 -> SUB [2]
  //   011 -> LW [3]
  //   100 -> AND [4] 
  //   101 -> OR [5] 
  //   110 -> CMP [6]
  //   111 -> SW [7] 
endmodule

module Somador_Subtrator (
  input  in_1,
  input  [7:0] Operando_1,
  input  [7:0] Operando_2,
  output [7:0] resultado,
  output Flag
);

  wire adder_1_cout, adder_2_cout, adder_3_cout, adder_4_cout, adder_5_cout, adder_6_cout, adder_7_cout,
       adder_8_cout, xor_1_out, xor_2_out, xor_3_out, xor_4_out, xor_5_out, xor_6_out, xor_7_out, xor_8_out;

  xor xor_1 (xor_1_out, Operando_2[0], in_1);
  xor xor_2 (xor_2_out, Operando_2[1], in_1);
  xor xor_3 (xor_3_out, Operando_2[2], in_1);
  xor xor_4 (xor_4_out, Operando_2[3], in_1);
  xor xor_5 (xor_5_out, Operando_2[4], in_1);
  xor xor_6 (xor_6_out, Operando_2[5], in_1);
  xor xor_7 (xor_7_out, Operando_2[6], in_1);
  xor xor_8 (xor_8_out, Operando_2[7], in_1);
  Adder #(.width(1)) adder_1 (.a(xor_1_out), .b(Operando_1[0]), .out(resultado[0]), .cin(in_1), .cout(adder_1_cout));
  Adder #(.width(1)) adder_2 (
    .a(xor_2_out), .b(Operando_1[1]), .out(resultado[1]), .cin(adder_1_cout), .cout(adder_2_cout));
  Adder #(.width(1)) adder_3 (
    .a(xor_3_out), .b(Operando_1[2]), .out(resultado[2]), .cin(adder_2_cout), .cout(adder_3_cout));
  Adder #(.width(1)) adder_4 (
    .a(xor_4_out), .b(Operando_1[3]), .out(resultado[3]), .cin(adder_3_cout), .cout(adder_4_cout));
  Adder #(.width(1)) adder_5 (
    .a(xor_5_out), .b(Operando_1[4]), .out(resultado[4]), .cin(adder_4_cout), .cout(adder_5_cout));
  Adder #(.width(1)) adder_6 (
    .a(xor_6_out), .b(Operando_1[5]), .out(resultado[5]), .cin(adder_5_cout), .cout(adder_6_cout));
  Adder #(.width(1)) adder_7 (
    .a(xor_7_out), .b(Operando_1[6]), .out(resultado[6]), .cin(adder_6_cout), .cout(adder_7_cout));
  Adder #(.width(1)) adder_8 (
    .a(xor_8_out), .b(Operando_1[7]), .out(resultado[7]), .cin(adder_7_cout), .cout(adder_8_cout));
  xor xor_9 (Flag, adder_8_cout, adder_7_cout);
  LED led_1 (.in(Flag));
  LED led_2 (.in(resultado[7]));
  LED led_3 (.in(resultado[6]));
  LED led_4 (.in(resultado[5]));
  LED led_5 (.in(resultado[4]));
  LED led_6 (.in(resultado[2]));
  LED led_7 (.in(resultado[1]));
  LED led_8 (.in(resultado[3]));
  LED led_9 (.in(resultado[0]));

  // Other names for the same wires on the sheet: op = in_1

  // Notes on the sheet:
  //   Operando_1: pull=down
  //   resultado: pull=down
  //   Operando_2: pull=down
endmodule

module AND (
  input  [7:0] in_1,
  input  [7:0] in_2,
  output [7:0] resultado
);

  and and_1 (resultado[0], in_1[0], in_2[0]);
  and and_2 (resultado[1], in_1[1], in_2[1]);
  and and_3 (resultado[2], in_1[2], in_2[2]);
  and and_4 (resultado[3], in_1[3], in_2[3]);
  and and_5 (resultado[4], in_1[4], in_2[4]);
  and and_6 (resultado[5], in_1[5], in_2[5]);
  and and_7 (resultado[6], in_1[6], in_2[6]);
  and and_8 (resultado[7], in_1[7], in_2[7]);
  LED led_1 (.in(resultado[7]));
  LED led_2 (.in(resultado[6]));
  LED led_3 (.in(resultado[4]));
  LED led_4 (.in(resultado[5]));
  LED led_5 (.in(resultado[1]));
  LED led_6 (.in(resultado[2]));
  LED led_7 (.in(resultado[3]));
  LED led_8 (.in(resultado[0]));

  // Other names for the same wires on the sheet: operando_1[7:0] = in_1; operando_2[7:0] = in_2
endmodule

module OR (
  input  [7:0] in_1,
  input  [7:0] in_2,
  output [7:0] resultado
);

  or or_1 (resultado[0], in_1[0], in_2[0]);
  or or_2 (resultado[1], in_1[1], in_2[1]);
  or or_3 (resultado[2], in_1[2], in_2[2]);
  or or_4 (resultado[3], in_1[3], in_2[3]);
  or or_5 (resultado[4], in_1[4], in_2[4]);
  or or_6 (resultado[5], in_1[5], in_2[5]);
  or or_7 (resultado[6], in_1[6], in_2[6]);
  or or_8 (resultado[7], in_1[7], in_2[7]);
  LED led_1 (.in(resultado[6]));
  LED led_2 (.in(resultado[7]));
  LED led_3 (.in(resultado[5]));
  LED led_4 (.in(resultado[4]));
  LED led_5 (.in(resultado[1]));
  LED led_6 (.in(resultado[2]));
  LED led_7 (.in(resultado[3]));
  LED led_8 (.in(resultado[0]));

  // Other names for the same wires on the sheet: operando_1[7:0] = in_1; operando_2[7:0] = in_2
endmodule
