// Logisim project bancoRegistradores.circ as structural Verilog: 5 circuits, main circuit main
module main (
  input  \Endereço_1 ,
  input  in_2,
  input  in_3,
  input  R_W,
  input  Clear,
  input  \Endereço_2 ,
  input  in_7,
  input  in_8,
  input  \Endereço_3 ,
  input  in_10,
  input  in_11,
  input  Dado_Escrito,
  input  in_13,
  input  in_14,
  input  in_15,
  input  in_16,
  input  in_17,
  input  in_18,
  input  in_19,
  output out_20,
  output out_21,
  output out_22,
  output out_23,
  output out_24,
  output out_25,
  output out_26,
  output Dado_Lido_1,
  output out_28,
  output out_29,
  output out_30,
  output out_31,
  output out_32,
  output out_33,
  output out_34,
  output Dado_Lido_2
);

  wire clock_1_out;

  Banco_registradores_write_read_paralelo banco_registradores_write_read_paralelo_1 (
    .Fonte1({\Endereço_1 , in_2, in_3}), .Fonte2({\Endereço_2 , in_7, in_8}),
    .Dado__a_ser_Escrito({Dado_Escrito, in_13, in_14, in_15, in_16, in_17, in_18, in_19}), .clear(Clear),
    .Dado_1({out_20, out_21, out_22, out_23, out_24, out_25, out_26, Dado_Lido_1}),
    .Fonte3({\Endereço_3 , in_10, in_11}),
    .Dado_2({out_28, out_29, out_30, out_31, out_32, out_33, out_34, Dado_Lido_2}), .Read(R_W),
    .Clock(clock_1_out), .Write(R_W));
  Clock clock_1 (.out(clock_1_out));
  Banco_registradores_Mini_Mips8Bits_sMux banco_registradores_mini_mips8bits_smux_1 ();  // open: Read_Register_1, Read_Register_2, Write_data, RegWrite, Write_Register, Clock, Clear, Read_data_1, Read_data_2

  // Notes on the sheet:
  //   in_19: pull=up
  //   out_33: pull=up
  //   out_23: pull=up
  //   out_22: pull=up
  //   Dado_Escrito: pull=up
  //   out_29: pull=up
  //   in_10: pull=up
  //   in_7: pull=up
  //   Endereço_2: pull=up
  //   out_21: pull=up
  //   in_2: pull=up
  //   out_28: pull=up
  //   in_18: pull=up
  //   out_24: pull=up
  //   out_34: pull=up
  //   in_13: pull=up
  //   out_26: pull=up
  //   in_11: pull=up
  //   Endereço_1: pull=up
  //   in_15: pull=up
  //   out_30: pull=up
  //   Dado_Lido_1: pull=up
  //   out_32: pull=up
  //   out_20: pull=up
  //   out_31: pull=up
  //   in_16: pull=up
  //   in_17: pull=up
  //   out_25: pull=up
  //   Dado_Lido_2: pull=up
  //   in_8: pull=up
  //   in_14: pull=up
  //   in_3: pull=up
  //   Endereço_3: pull=up
endmodule

// B. Reg
module Banco_registradores_write_read_serie (
  input  [2:0] Fonte1,
  input  [2:0] Fonte2,
  input  _1___Leitura___Escrita___0,
  input  [2:0] Fonte3,
  input  [7:0] Dado__a_ser_Escrito,
  input  clear,
  input  Clock,
  output [7:0] Dado_1,
  output [7:0] Dado_2
);

  wire not_1_out, not_2_out, not_3_out;
  wire [2:0] multiplexer_1_out, multiplexer_2_out;

  Multiplexer #(.width(3), .disabled(0), .enable("false")) multiplexer_1 (
    .in0(Fonte1), .in1(Fonte3), .out(multiplexer_1_out), .sel(not_1_out));
  Multiplexer #(.width(3), .disabled(0), .enable("false")) multiplexer_2 (
    .in0(Fonte2), .in1(Fonte3), .out(multiplexer_2_out), .sel(not_2_out));
  not not_1 (not_1_out, _1___Leitura___Escrita___0);
  not not_2 (not_2_out, _1___Leitura___Escrita___0);
  not not_3 (not_3_out, _1___Leitura___Escrita___0);
  RAM #(.addrWidth(3), .bus("separate")) ram_1 (
    .addr(multiplexer_1_out), .din(Dado__a_ser_Escrito), .data(Dado_1), .str(not_1_out), .clk(Clock),
    .ld(_1___Leitura___Escrita___0), .clr(clear));  // open: sel
  RAM #(.addrWidth(3), .bus("separate")) ram_2 (
    .addr(multiplexer_2_out), .din(Dado__a_ser_Escrito), .data(Dado_2), .str(not_2_out), .clk(Clock),
    .ld(_1___Leitura___Escrita___0), .clr(clear));  // open: sel
  RAM #(.addrWidth(3), .bus("separate")) ram_3 (
    .addr(Fonte3), .din(Dado__a_ser_Escrito), .str(not_3_out), .clk(Clock), .ld(_1___Leitura___Escrita___0),
    .clr(clear));  // open: data, sel

  // Other names for the same wires on the sheet: clk = Clock; rw = _1___Leitura___Escrita___0

  // Notes on the sheet:
  //   Dado_2: pull=up
  //   Fonte1: pull=up
  //   Fonte2: pull=up
  //   Dado_1: pull=up
  //   clear: pull=up
  //   _1___Leitura___Escrita___0: pull=up
  //   Fonte3: pull=up
  //   Dado__a_ser_Escrito: pull=up
endmodule

// B. REG
module Banco_registradores_write_read_paralelo (
  input  [2:0] Fonte1,
  input  [2:0] Fonte2,
  input  [2:0] Fonte3,
  input  [7:0] Dado__a_ser_Escrito,
  input  Write,
  input  Clock,
  input  Read,
  input  clear,
  output [7:0] Dado_1,
  output [7:0] Dado_2
);

  wire [2:0] multiplexer_1_out, multiplexer_2_out;

  Multiplexer #(.width(3), .disabled(0), .enable("false")) multiplexer_1 (
    .in0(Fonte1), .in1(Fonte3), .out(multiplexer_1_out), .sel(Write));
  Multiplexer #(.width(3), .disabled(0), .enable("false")) multiplexer_2 (
    .in0(Fonte2), .in1(Fonte3), .out(multiplexer_2_out), .sel(Write));
  RAM #(.addrWidth(3), .bus("separate")) ram_1 (
    .addr(multiplexer_1_out), .din(Dado__a_ser_Escrito), .data(Dado_1), .str(Write), .clk(Clock), .ld(Read),
    .clr(clear));  // open: sel
  RAM #(.addrWidth(3), .bus("separate")) ram_2 (
    .addr(multiplexer_2_out), .din(Dado__a_ser_Escrito), .data(Dado_2), .str(Write), .clk(Clock), .ld(Read),
    .clr(clear));  // open: sel
  RAM #(.addrWidth(3), .bus("separate")) ram_3 (
    .addr(Fonte3), .din(Dado__a_ser_Escrito), .str(Write), .clk(Clock), .ld(Read), .clr(clear));  // open: data, sel

  // Other names for the same wires on the sheet: clk = Clock; R = Read; W = Write

  // Notes on the sheet:
  //   Fonte2: pull=up
  //   Dado_1: pull=up
  //   Dado__a_ser_Escrito: pull=up
  //   Dado_2: pull=up
  //   Read: pull=down
  //   Fonte1: pull=up
  //   Clock: pull=down
  //   clear: pull=down
  //   Fonte3: pull=up
  //   Write: pull=down
endmodule

// B. REG
module Banco_registradores_Mini_MIPS8_cMux (
  input  [2:0] Read_Register_1,
  input  [2:0] Read_Register_2,
  input  [7:0] Write_data,
  input  [2:0] Write_Register,
  input  RegWrite,
  input  Clock,
  input  Clear,
  output [7:0] Read_data_1,
  output [7:0] Read_data_2
);

  wire WE0, WE1, WE2, WE3, WE4, WE5, WE6, WE7;
  wire [7:0] demultiplexer_2_out0, demultiplexer_2_out1, demultiplexer_2_out2, demultiplexer_2_out3,
       demultiplexer_2_out4, demultiplexer_2_out5, demultiplexer_2_out6, demultiplexer_2_out7, Reg0, Reg1,
       Reg2, Reg3, Reg4, Reg5, Reg6, Reg7;

  Demultiplexer #(.select(3)) demultiplexer_1 (
    .out0(WE0), .out1(WE1), .out2(WE2), .out3(WE3), .out4(WE4), .out5(WE5), .out6(WE6), .out7(WE7),
    .in(RegWrite), .sel(Write_Register));  // open: en
  Demultiplexer #(.select(3), .width(8)) demultiplexer_2 (
    .out0(demultiplexer_2_out0), .out1(demultiplexer_2_out1), .out2(demultiplexer_2_out2),
    .out3(demultiplexer_2_out3), .out4(demultiplexer_2_out4), .out5(demultiplexer_2_out5),
    .out6(demultiplexer_2_out6), .out7(demultiplexer_2_out7), .in(Write_data), .sel(Write_Register));  // open: en
  Register u_Reg0 (.D(demultiplexer_2_out0), .en(WE0), .Q(Reg0), .clk(Clock), .clr(Clear));
  Register u_Reg1 (.D(demultiplexer_2_out1), .en(WE1), .Q(Reg1), .clk(Clock), .clr(Clear));
  Register u_Reg2 (.D(demultiplexer_2_out2), .en(WE2), .Q(Reg2), .clk(Clock), .clr(Clear));
  Register u_Reg3 (.D(demultiplexer_2_out3), .en(WE3), .Q(Reg3), .clk(Clock), .clr(Clear));
  Register u_Reg4 (.D(demultiplexer_2_out4), .en(WE4), .Q(Reg4), .clk(Clock), .clr(Clear));
  Register u_Reg5 (.D(demultiplexer_2_out5), .en(WE5), .Q(Reg5), .clk(Clock), .clr(Clear));
  Register u_Reg6 (.D(demultiplexer_2_out6), .en(WE6), .Q(Reg6), .clk(Clock), .clr(Clear));
  Register u_Reg7 (.D(demultiplexer_2_out7), .en(WE7), .Q(Reg7), .clk(Clock), .clr(Clear));
  Multiplexer #(.select(3), .width(8)) multiplexer_1 (
    .in0(Reg0), .in1(Reg1), .in2(Reg2), .in3(Reg3), .in4(Reg4), .in5(Reg5), .in6(Reg6), .in7(Reg7),
    .out(Read_data_1), .sel(Read_Register_1));  // open: en
  Multiplexer #(.select(3), .width(8)) multiplexer_2 (
    .in0(Reg0), .in1(Reg1), .in2(Reg2), .in3(Reg3), .in4(Reg4), .in5(Reg5), .in6(Reg6), .in7(Reg7),
    .out(Read_data_2), .sel(Read_Register_2));  // open: en

  // Other names for the same wires on the sheet: Read1[2:0] = Read_Register_1; Read2[2:0] = Read_Register_2

  // Notes on the sheet:
  //   Clear: pull=down
  //   RegWrite: pull=down
  //   Clock: pull=down
  //   Read_data_1: pull=down
  //   Read_data_2: pull=down
endmodule

// B. REG
module Banco_registradores_Mini_Mips8Bits_sMux (
  input  [2:0] Read_Register_1,
  input  [2:0] Read_Register_2,
  input  [7:0] Write_data,
  input  RegWrite,
  input  [2:0] Write_Register,
  input  Clock,
  input  Clear,
  output [7:0] Read_data_1,
  output [7:0] Read_data_2
);

  wire WE0, WE1, WE2, WE3, WE4, WE5, WE6, WE7;
  wire [7:0] Reg0, Reg1, Reg2, Reg3, Reg4, Reg5, Reg6, Reg7;

  Demultiplexer #(.select(3)) demultiplexer_1 (
    .out0(WE0), .out1(WE1), .out2(WE2), .out3(WE3), .out4(WE4), .out5(WE5), .out6(WE6), .out7(WE7),
    .in(RegWrite), .sel(Write_Register));  // open: en
  Register u_Reg0 (.D(Write_data), .en(WE0), .Q(Reg0), .clk(Clock), .clr(Clear));
  Register u_Reg1 (.D(Write_data), .en(WE1), .Q(Reg1), .clk(Clock), .clr(Clear));
  Register u_Reg2 (.D(Write_data), .en(WE2), .Q(Reg2), .clk(Clock), .clr(Clear));
  Register u_Reg3 (.D(Write_data), .en(WE3), .Q(Reg3), .clk(Clock), .clr(Clear));
  Register u_Reg4 (.D(Write_data), .en(WE4), .Q(Reg4), .clk(Clock), .clr(Clear));
  Register u_Reg5 (.D(Write_data), .en(WE5), .Q(Reg5), .clk(Clock), .clr(Clear));
  Register u_Reg6 (.D(Write_data), .en(WE6), .Q(Reg6), .clk(Clock), .clr(Clear));
  Register u_Reg7 (.D(Write_data), .en(WE7), .Q(Reg7), .clk(Clock), .clr(Clear));
  Multiplexer #(.select(3), .width(8)) multiplexer_1 (
    .in0(Reg0), .in1(Reg1), .in2(Reg2), .in3(Reg3), .in4(Reg4), .in5(Reg5), .in6(Reg6), .in7(Reg7),
    .out(Read_data_1), .sel(Read_Register_1));  // open: en
  Multiplexer #(.select(3), .width(8)) multiplexer_2 (
    .in0(Reg0), .in1(Reg1), .in2(Reg2), .in3(Reg3), .in4(Reg4), .in5(Reg5), .in6(Reg6), .in7(Reg7),
    .out(Read_data_2), .sel(Read_Register_2));  // open: en

  // Other names for the same wires on the sheet: Read1[2:0] = Read_Register_1; Read2[2:0] = Read_Register_2

  // Notes on the sheet:
  //   Read_data_1: pull=down
  //   Clock: pull=down
  //   Clear: pull=down
  //   RegWrite: pull=down
  //   Read_data_2: pull=down
endmodule
