// Logisim project controleMonocicplo.circ as structural Verilog: 2 circuits, main circuit main
module main (
  input  [3:0] OPCODE,
  input  [2:0] FUNCT,
  output Branch,
  output Jump,
  output incPC,
  output RegDst,
  output UlaFonte,
  output MemParaReg,
  output EscReg,
  output EscMem,
  output ControleUla2,
  output ControleUla1,
  output ControleUla0
);

  ControleMiniMips controleminimips_1 (
    .OP3(OPCODE[3]), .Branch(Branch), .OP2(OPCODE[2]), .OP1(OPCODE[1]), .Jump(Jump), .OP0(OPCODE[0]),
    .Funct2(FUNCT[2]), .IncPC(incPC), .Funct1(FUNCT[1]), .RegDst(RegDst), .Funct0(FUNCT[0]),
    .UlaFonte(UlaFonte), .MemParaReg(MemParaReg), .EscReg(EscReg), .EscMem(EscMem),
    .ControleUla2(ControleUla2), .ControleUla1(ControleUla1), .ControleUla0(ControleUla0));

  // Notes on the sheet:
  //   Jump: pull=down
  //   RegDst: pull=down
  //   ControleUla2: pull=down
  //   EscReg: pull=down
  //   incPC: pull=down
  //   EscMem: pull=down
  //   UlaFonte: pull=down
  //   ControleUla0: pull=down
  //   OPCODE: pull=down
  //   MemParaReg: pull=down
  //   ControleUla1: pull=down
  //   FUNCT: pull=down
  //   Branch: pull=down
endmodule

// CONTROLE MINI-MIPS
module ControleMiniMips (
  input  OP3,
  input  OP2,
  input  OP1,
  input  OP0,
  input  Funct2,
  input  Funct1,
  input  Funct0,
  output Branch,
  output Jump,
  output IncPC,
  output RegDst,
  output UlaFonte,
  output MemParaReg,
  output EscReg,
  output EscMem,
  output ControleUla2,
  output ControleUla1,
  output ControleUla0
);

  wire and_1_out, and_2_out, and_3_out, and_4_out, and_5_out, and_6_out, and_7_out, and_9_out, and_10_out,
       and_12_out, and_13_out, and_14_out, and_18_out, and_19_out, and_20_out, and_21_out, and_22_out,
       and_23_out, and_24_out, and_25_out, and_26_out, and_27_out, and_28_out, and_29_out, and_30_out,
       and_31_out, and_32_out, and_33_out, and_34_out, not_1_out, not_2_out, not_3_out, not_4_out, not_5_out,
       not_6_out, not_7_out, not_8_out, not_9_out, not_10_out, not_11_out, not_12_out, not_13_out,
       not_14_out, not_15_out, not_16_out, not_17_out, not_18_out, not_19_out, not_20_out, not_21_out,
       not_22_out, not_23_out, not_24_out, not_25_out, not_26_out, not_27_out, not_28_out, not_29_out,
       not_30_out, not_31_out, or_2_out, or_4_out, or_5_out, or_6_out;

  not not_1 (not_1_out, OP2);
  not not_2 (not_2_out, OP1);
  not not_3 (not_3_out, OP0);
  not not_4 (not_4_out, OP3);
  not not_5 (not_5_out, OP2);
  not not_6 (not_6_out, OP0);
  not not_7 (not_7_out, OP3);
  not not_8 (not_8_out, OP2);
  or or_1 (UlaFonte, OP0, OP2);
  not not_9 (not_9_out, OP3);
  not not_10 (not_10_out, OP1);
  not not_11 (not_11_out, OP3);
  not not_12 (not_12_out, OP1);
  not not_13 (not_13_out, OP3);
  not not_14 (not_14_out, OP1);
  and and_1 (and_1_out, OP3, OP2);
  and and_2 (and_2_out, OP1, OP0);
  not not_15 (not_15_out, OP2);
  not not_16 (not_16_out, OP1);
  not not_17 (not_17_out, OP2);
  not not_18 (not_18_out, OP1);
  not not_19 (not_19_out, OP3);
  not not_20 (not_20_out, OP1);
  and and_3 (and_3_out, OP3, not_1_out);
  and and_4 (and_4_out, not_2_out, not_3_out);
  and and_5 (and_5_out, not_4_out, not_5_out);
  and and_6 (and_6_out, OP1, not_6_out);
  and and_7 (and_7_out, not_7_out, not_8_out);
  not not_21 (not_21_out, OP1);
  and and_8 (MemParaReg, not_9_out, not_10_out);
  and and_9 (and_9_out, not_11_out, not_12_out);
  not not_22 (not_22_out, OP0);
  not not_23 (not_23_out, Funct2);
  not not_24 (not_24_out, Funct0);
  and and_10 (and_10_out, not_13_out, not_14_out);
  not not_25 (not_25_out, OP0);
  not not_26 (not_26_out, Funct1);
  not not_27 (not_27_out, OP3);
  not not_28 (not_28_out, OP1);
  not not_29 (not_29_out, OP0);
  not not_30 (not_30_out, OP2);
  and and_11 (EscMem, and_1_out, and_2_out);
  and and_12 (and_12_out, not_15_out, not_16_out);
  and and_13 (and_13_out, not_17_out, not_18_out);
  and and_14 (and_14_out, not_19_out, not_20_out);
  and and_15 (Branch, and_3_out, and_4_out);
  and and_16 (Jump, and_5_out, and_6_out);
  and and_17 (RegDst, and_7_out, not_21_out);
  and and_18 (and_18_out, and_9_out, not_22_out);
  and and_19 (and_19_out, not_23_out, not_24_out);
  and and_20 (and_20_out, and_10_out, not_25_out);
  and and_21 (and_21_out, Funct2, not_26_out);
  and and_22 (and_22_out, not_27_out, OP2);
  and and_23 (and_23_out, not_28_out, not_29_out);
  and and_24 (and_24_out, OP3, not_30_out);
  and and_25 (and_25_out, OP1, OP0);
  and and_26 (and_26_out, and_12_out, Funct2);
  and and_27 (and_27_out, OP2, OP1);
  not not_31 (not_31_out, OP0);
  and and_28 (and_28_out, and_13_out, Funct1);
  and and_29 (and_29_out, and_14_out, Funct0);
  and and_30 (and_30_out, and_18_out, and_19_out);
  and and_31 (and_31_out, and_20_out, and_21_out);
  and and_32 (and_32_out, and_22_out, and_23_out);
  and and_33 (and_33_out, and_24_out, and_25_out);
  or or_2 (or_2_out, and_26_out, and_27_out);
  and and_34 (and_34_out, OP3, not_31_out);
  or or_3 (ControleUla1, and_28_out, OP3);
  or or_4 (or_4_out, and_29_out, OP0);
  or or_5 (or_5_out, and_30_out, and_31_out);
  or or_6 (or_6_out, and_32_out, and_33_out);
  or or_7 (ControleUla2, or_2_out, and_34_out);
  or or_8 (ControleUla0, or_4_out, OP2);
  or or_9 (EscReg, or_5_out, or_6_out);

  assign IncPC = 1'b1;
endmodule
