// Logisim project controleMulticiclo.circ as structural Verilog: 6 circuits, main circuit main
module main (
  input  Op3,
  input  Op2,
  input  Op1,
  input  Op0,
  input  Funct2,
  input  Funct1,
  input  Funct0,
  input  Clear,
  output ControleUla2,
  output ControleUla1,
  output ControleUla0,
  output PCEsc,
  output Branch,
  output IouD,
  output EscMem,
  output IREsc,
  output MemParaReg,
  output RegDst,
  output EscReg,
  output UlaFonteA,
  output UlaFonteB1,
  output UlaFonteB0,
  output PCFonte1,
  output PCFonte0,
  output [3:0] Estado
);

  wire clock_1_out;

  Clock clock_1 (.out(clock_1_out));
  Controle_Multiciclo controle_multiciclo_1 (
    .Op3(Op3), .Op2(Op2), .Op1(Op1), .Op0(Op0), .Funct2(Funct2), .Funct1(Funct1), .Funct0(Funct0),
    .Clock(clock_1_out), .Clear(Clear), .ControleUla2(ControleUla2), .Branch(Branch),
    .ControleUla1(ControleUla1), .PCEsc(PCEsc), .ControleUla0(ControleUla0), .IouD(IouD), .EscMem(EscMem),
    .IREsc(IREsc), .MemParaReg(MemParaReg), .RegDst(RegDst), .EscReg(EscReg), .UlaFonteA(UlaFonteA),
    .UlaFonteB1(UlaFonteB1), .UlaFonteB0(UlaFonteB0), .PCFonte1(PCFonte1), .PCFonte0(PCFonte0),
    .E3(Estado[3]), .E2(Estado[2]), .E1(Estado[1]), .E0(Estado[0]));
  Hex_Digit_Display hex_digit_display_1 (.value(Estado));  // open: dp
endmodule

module Controle_Estados (
  input  E3,
  input  E2,
  input  E1,
  input  E0,
  input  Op3,
  input  Op2,
  input  Op1,
  input  Op0,
  output Ep3,
  output Ep2,
  output Ep1,
  output Ep0
);

  wire and_1_out, and_2_out, and_3_out, and_4_out, and_5_out, and_6_out, and_7_out, and_8_out, and_9_out,
       and_10_out, and_11_out, and_12_out, and_13_out, and_14_out, and_15_out, and_16_out, and_17_out,
       and_18_out, and_19_out, and_20_out, and_21_out, and_22_out, and_23_out, and_24_out, and_25_out,
       and_26_out, and_27_out, and_28_out, and_29_out, and_30_out, and_31_out, and_32_out, and_33_out,
       and_34_out, and_35_out, and_36_out, and_37_out, and_38_out, and_39_out, and_40_out, and_41_out,
       and_42_out, and_43_out, and_44_out, and_45_out, and_46_out, and_47_out, not_1_out, not_2_out,
       not_3_out, not_4_out, not_5_out, not_6_out, not_7_out, not_8_out, not_9_out, not_10_out, not_11_out,
       not_12_out, not_13_out, not_14_out, not_15_out, not_16_out, not_17_out, not_18_out, not_19_out,
       not_20_out, not_21_out, not_22_out, not_23_out, not_24_out, not_25_out, not_26_out, not_27_out,
       not_28_out, not_29_out, not_30_out, not_31_out, not_32_out, not_33_out, not_34_out, not_35_out,
       not_36_out, not_37_out, not_38_out, not_39_out, not_40_out, not_41_out, not_42_out, or_1_out,
       or_2_out, or_3_out, or_4_out, or_7_out, or_8_out;

  and and_1 (and_1_out, E0, not_1_out);
  not not_1 (not_1_out, Op3);
  not not_2 (not_2_out, Op2);
  not not_3 (not_3_out, Op0);
  not not_4 (not_4_out, E3);
  and and_2 (and_2_out, not_4_out, E0);
  not not_5 (not_5_out, Op2);
  and and_3 (and_3_out, not_5_out, not_6_out);
  not not_6 (not_6_out, Op1);
  not not_7 (not_7_out, Op0);
  not not_8 (not_8_out, E2);
  and and_4 (and_4_out, not_8_out, E0);
  not not_9 (not_9_out, Op3);
  not not_10 (not_10_out, Op2);
  and and_5 (and_5_out, not_10_out, not_11_out);
  not not_11 (not_11_out, Op1);
  not not_12 (not_12_out, Op0);
  not not_13 (not_13_out, E2);
  not not_14 (not_14_out, E2);
  and and_6 (and_6_out, not_14_out, E0);
  not not_15 (not_15_out, Op3);
  not not_16 (not_16_out, Op2);
  not not_17 (not_17_out, Op0);
  not not_18 (not_18_out, E2);
  and and_7 (and_7_out, not_18_out, E0);
  not not_19 (not_19_out, Op3);
  not not_20 (not_20_out, Op1);
  not not_21 (not_21_out, Op0);
  not not_22 (not_22_out, E2);
  not not_23 (not_23_out, E1);
  not not_24 (not_24_out, E3);
  not not_25 (not_25_out, E2);
  not not_26 (not_26_out, E1);
  not not_27 (not_27_out, E0);
  not not_28 (not_28_out, E3);
  and and_8 (and_8_out, not_28_out, not_29_out);
  not not_29 (not_29_out, E1);
  not not_30 (not_30_out, Op2);
  not not_31 (not_31_out, Op1);
  not not_32 (not_32_out, Op0);
  and and_9 (and_9_out, and_1_out, not_2_out);
  and and_10 (and_10_out, Op1, not_3_out);
  and and_11 (and_11_out, and_2_out, Op3);
  and and_12 (and_12_out, and_3_out, not_7_out);
  not not_33 (not_33_out, Op3);
  and and_13 (and_13_out, and_4_out, not_9_out);
  and and_14 (and_14_out, and_5_out, not_12_out);
  and and_15 (and_15_out, not_13_out, E1);
  not not_34 (not_34_out, E2);
  and and_16 (and_16_out, and_6_out, not_15_out);
  and and_17 (and_17_out, not_16_out, not_17_out);
  and and_18 (and_18_out, and_7_out, not_19_out);
  and and_19 (and_19_out, not_20_out, not_21_out);
  and and_20 (and_20_out, not_22_out, not_23_out);
  and and_21 (and_21_out, Op3, Op1);
  not not_35 (not_35_out, E3);
  not not_36 (not_36_out, E0);
  not not_37 (not_37_out, Op2);
  not not_38 (not_38_out, E2);
  and and_22 (and_22_out, not_24_out, not_25_out);
  and and_23 (and_23_out, not_26_out, not_27_out);
  and and_24 (and_24_out, and_8_out, not_30_out);
  and and_25 (and_25_out, not_31_out, not_32_out);
  not not_39 (not_39_out, E2);
  not not_40 (not_40_out, E0);
  and and_26 (and_26_out, and_9_out, and_10_out);
  and and_27 (and_27_out, and_11_out, and_12_out);
  and and_28 (and_28_out, E2, not_33_out);
  not not_41 (not_41_out, Op2);
  and and_29 (and_29_out, and_13_out, and_14_out);
  and and_30 (and_30_out, and_15_out, Op2);
  and and_31 (and_31_out, not_34_out, E1);
  and and_32 (and_32_out, and_16_out, and_17_out);
  and and_33 (and_33_out, and_18_out, and_19_out);
  and and_34 (and_34_out, and_20_out, E0);
  and and_35 (and_35_out, and_21_out, Op0);
  and and_36 (and_36_out, not_35_out, E1);
  and and_37 (and_37_out, not_36_out, not_37_out);
  and and_38 (and_38_out, not_38_out, E1);
  not not_42 (not_42_out, Op1);
  and and_39 (and_39_out, and_22_out, and_23_out);
  and and_40 (and_40_out, and_24_out, and_25_out);
  and and_41 (and_41_out, not_39_out, not_40_out);
  or or_1 (or_1_out, and_26_out, and_27_out);
  and and_42 (and_42_out, and_28_out, not_41_out);
  or or_2 (or_2_out, and_29_out, and_30_out);
  and and_43 (and_43_out, and_31_out, E0);
  or or_3 (or_3_out, and_32_out, and_33_out);
  and and_44 (and_44_out, and_34_out, and_35_out);
  and and_45 (and_45_out, and_36_out, and_37_out);
  and and_46 (and_46_out, and_38_out, not_42_out);
  or or_4 (or_4_out, and_39_out, and_40_out);
  and and_47 (and_47_out, and_41_out, Op0);
  or or_5 (Ep3, or_1_out, and_42_out);
  or or_6 (Ep2, or_2_out, and_43_out);
  or or_7 (or_7_out, or_3_out, and_44_out);
  or or_8 (or_8_out, and_45_out, and_46_out);
  or or_9 (Ep0, or_4_out, and_47_out);
  or or_10 (Ep1, or_7_out, or_8_out);
endmodule

// Controle ULA
module Controle_ULA (
  input  E3,
  input  E2,
  input  E1,
  input  E0,
  input  Funct2,
  input  Funct1,
  input  Funct0,
  output ControleUla2,
  output ControleUla1,
  output ControleUla0
);

  wire and_1_out, and_2_out, and_3_out, and_4_out, and_5_out, and_6_out, and_7_out, and_8_out, and_9_out,
       and_10_out, and_11_out, and_12_out, and_13_out, and_14_out, and_15_out, and_16_out, and_17_out,
       and_18_out, and_19_out, and_20_out, and_21_out, and_22_out, and_23_out, not_1_out, not_2_out,
       not_3_out, not_4_out, not_5_out, not_6_out, not_7_out, or_1_out, or_2_out, or_3_out, or_4_out;

  not not_1 (not_1_out, E2);
  not not_2 (not_2_out, E2);
  not not_3 (not_3_out, E2);
  not not_4 (not_4_out, E2);
  not not_5 (not_5_out, E2);
  and and_1 (and_1_out, E2, E1);
  and and_2 (and_2_out, E0, Funct2);
  and and_3 (and_3_out, E3, not_1_out);
  and and_4 (and_4_out, E3, not_2_out);
  and and_5 (and_5_out, E2, E1);
  and and_6 (and_6_out, E0, Funct1);
  and and_7 (and_7_out, E3, not_3_out);
  and and_8 (and_8_out, E3, not_4_out);
  and and_9 (and_9_out, E3, not_5_out);
  not not_6 (not_6_out, E1);
  not not_7 (not_7_out, E0);
  and and_10 (and_10_out, and_1_out, and_2_out);
  and and_11 (and_11_out, and_3_out, Funct2);
  and and_12 (and_12_out, E3, E0);
  and and_13 (and_13_out, and_4_out, E1);
  and and_14 (and_14_out, and_5_out, and_6_out);
  and and_15 (and_15_out, and_7_out, Funct1);
  and and_16 (and_16_out, E3, E0);
  and and_17 (and_17_out, and_8_out, E1);
  and and_18 (and_18_out, E2, E1);
  and and_19 (and_19_out, E0, Funct0);
  and and_20 (and_20_out, and_9_out, not_6_out);
  and and_21 (and_21_out, not_7_out, Funct0);
  or or_1 (or_1_out, and_10_out, and_11_out);
  or or_2 (or_2_out, and_12_out, and_13_out);
  or or_3 (or_3_out, and_14_out, and_15_out);
  or or_4 (or_4_out, and_16_out, and_17_out);
  and and_22 (and_22_out, and_18_out, and_19_out);
  and and_23 (and_23_out, and_20_out, and_21_out);
  or or_5 (ControleUla2, or_1_out, or_2_out);
  or or_6 (ControleUla1, or_3_out, or_4_out);
  or or_7 (ControleUla0, and_22_out, and_23_out);
endmodule

// Sinais
module Controle_Sinais (
  input  E3,
  input  E2,
  input  E1,
  input  E0,
  output Branch,
  output PCEsc,
  output IouD,
  output EscMem,
  output IREsc,
  output MemParaReg,
  output RegDst,
  output EscReg
);

  wire and_2_out, and_3_out, and_4_out, and_5_out, and_6_out, and_7_out, and_8_out, and_9_out, and_10_out,
       and_11_out, and_12_out, and_13_out, and_14_out, and_15_out, and_16_out, and_17_out, and_21_out,
       and_22_out, and_23_out, and_24_out, and_25_out, and_26_out, not_1_out, not_2_out, not_3_out,
       not_4_out, not_5_out, not_6_out, not_7_out, not_8_out, not_9_out, not_10_out, not_11_out, not_12_out,
       not_13_out, not_14_out, not_15_out, not_16_out, not_17_out, not_18_out, not_19_out, not_20_out,
       not_21_out, not_22_out, or_3_out;

  and and_1 (Branch, E3, E0);
  not not_1 (not_1_out, E3);
  and and_2 (and_2_out, not_1_out, not_2_out);
  not not_2 (not_2_out, E2);
  not not_3 (not_3_out, E1);
  and and_3 (and_3_out, not_3_out, not_4_out);
  not not_4 (not_4_out, E0);
  not not_5 (not_5_out, E2);
  and and_4 (and_4_out, not_5_out, E1);
  and and_5 (and_5_out, E2, not_6_out);
  not not_6 (not_6_out, E1);
  and and_6 (and_6_out, E2, not_7_out);
  not not_7 (not_7_out, E1);
  not not_8 (not_8_out, E3);
  and and_7 (and_7_out, not_8_out, not_9_out);
  not not_9 (not_9_out, E2);
  not not_10 (not_10_out, E1);
  and and_8 (and_8_out, not_10_out, not_11_out);
  not not_11 (not_11_out, E0);
  and and_9 (and_9_out, E2, not_12_out);
  not not_12 (not_12_out, E1);
  not not_13 (not_13_out, E0);
  not not_14 (not_14_out, E3);
  and and_10 (and_10_out, not_14_out, not_15_out);
  not not_15 (not_15_out, E2);
  not not_16 (not_16_out, E1);
  not not_17 (not_17_out, E3);
  and and_11 (and_11_out, not_17_out, E2);
  and and_12 (and_12_out, E1, E0);
  not not_18 (not_18_out, E1);
  not not_19 (not_19_out, E0);
  and and_13 (and_13_out, E3, not_20_out);
  not not_20 (not_20_out, E1);
  not not_21 (not_21_out, E0);
  and and_14 (and_14_out, and_2_out, and_3_out);
  and and_15 (and_15_out, E3, E1);
  and and_16 (and_16_out, and_4_out, E0);
  and and_17 (and_17_out, and_5_out, E0);
  and and_18 (EscMem, and_6_out, E0);
  and and_19 (IREsc, and_7_out, and_8_out);
  and and_20 (MemParaReg, and_9_out, not_13_out);
  and and_21 (and_21_out, and_10_out, not_16_out);
  and and_22 (and_22_out, and_11_out, and_12_out);
  and and_23 (and_23_out, E3, not_18_out);
  not not_22 (not_22_out, E0);
  and and_24 (and_24_out, E2, not_19_out);
  and and_25 (and_25_out, and_13_out, not_21_out);
  or or_1 (PCEsc, and_14_out, and_15_out);
  or or_2 (IouD, and_16_out, and_17_out);
  or or_3 (or_3_out, and_21_out, and_22_out);
  and and_26 (and_26_out, and_23_out, not_22_out);
  or or_4 (EscReg, and_24_out, and_25_out);
  or or_5 (RegDst, or_3_out, and_26_out);
endmodule

// Fonte/PC
module ULA_PC_Fonte (
  input  E3,
  input  E2,
  input  E1,
  input  E0,
  output UlaFonteA,
  output UlaFonteB1,
  output UlaFonteB0,
  output PCFonte1,
  output PCFonte0
);

  wire and_1_out, and_2_out, and_3_out, and_4_out, and_5_out, and_6_out, and_7_out, and_8_out, and_9_out,
       and_10_out, and_11_out, and_12_out, and_13_out, and_14_out, and_16_out, and_17_out, not_1_out,
       not_2_out, not_3_out, not_4_out, not_5_out, not_6_out, not_7_out, not_8_out, not_9_out, not_10_out,
       not_11_out, not_12_out, not_13_out, not_14_out, or_1_out, or_2_out, or_4_out, or_5_out;

  not not_1 (not_1_out, E3);
  and and_1 (and_1_out, not_1_out, E1);
  and and_2 (and_2_out, E3, not_2_out);
  not not_2 (not_2_out, E1);
  and and_3 (and_3_out, E3, E0);
  not not_3 (not_3_out, E3);
  and and_4 (and_4_out, not_3_out, not_4_out);
  not not_4 (not_4_out, E2);
  not not_5 (not_5_out, E3);
  and and_5 (and_5_out, not_5_out, not_6_out);
  not not_6 (not_6_out, E2);
  not not_7 (not_7_out, E1);
  not not_8 (not_8_out, E0);
  not not_9 (not_9_out, E3);
  and and_6 (and_6_out, not_9_out, not_10_out);
  not not_10 (not_10_out, E2);
  not not_11 (not_11_out, E1);
  and and_7 (and_7_out, not_11_out, not_12_out);
  not not_12 (not_12_out, E0);
  and and_8 (and_8_out, E3, not_13_out);
  not not_13 (not_13_out, E2);
  and and_9 (and_9_out, E3, E2);
  and and_10 (and_10_out, E3, not_14_out);
  not not_14 (not_14_out, E2);
  or or_1 (or_1_out, and_1_out, E2);
  or or_2 (or_2_out, and_2_out, and_3_out);
  and and_11 (and_11_out, and_4_out, E0);
  and and_12 (and_12_out, and_5_out, E1);
  and and_13 (and_13_out, E2, not_7_out);
  and and_14 (and_14_out, E2, not_8_out);
  and and_15 (UlaFonteB0, and_6_out, and_7_out);
  and and_16 (and_16_out, and_8_out, E1);
  and and_17 (and_17_out, and_9_out, E0);
  and and_18 (PCFonte0, and_10_out, E0);
  or or_3 (UlaFonteA, or_1_out, or_2_out);
  or or_4 (or_4_out, and_11_out, and_12_out);
  or or_5 (or_5_out, and_13_out, and_14_out);
  or or_6 (PCFonte1, and_16_out, and_17_out);
  or or_7 (UlaFonteB1, or_4_out, or_5_out);
endmodule

module Controle_Multiciclo (
  input  Op3,
  input  Op2,
  input  Op1,
  input  Op0,
  input  Funct2,
  input  Funct1,
  input  Funct0,
  input  Clock,
  input  Clear,
  output ControleUla2,
  output Branch,
  output ControleUla1,
  output PCEsc,
  output ControleUla0,
  output IouD,
  output EscMem,
  output IREsc,
  output MemParaReg,
  output RegDst,
  output EscReg,
  output UlaFonteA,
  output UlaFonteB1,
  output UlaFonteB0,
  output PCFonte1,
  output PCFonte0,
  output E3,
  output E2,
  output E1,
  output E0
);

  wire controle_estados_1_ep0, controle_estados_1_ep1, controle_estados_1_ep2, controle_estados_1_ep3;

  Controle_ULA controle_ula_1 (
    .E3(E3), .E2(E2), .E1(E1), .ControleUla2(ControleUla2), .E0(E0), .Funct2(Funct2), .Funct1(Funct1),
    .Funct0(Funct0), .ControleUla1(ControleUla1), .ControleUla0(ControleUla0));
  Controle_Estados controle_estados_1 (
    .E3(E3), .E2(E2), .E1(E1), .E0(E0), .Op3(Op3), .Ep3(controle_estados_1_ep3), .Op2(Op2), .Op1(Op1),
    .Op0(Op0), .Ep2(controle_estados_1_ep2), .Ep1(controle_estados_1_ep1), .Ep0(controle_estados_1_ep0));
  Controle_Sinais controle_sinais_1 (
    .E3(E3), .E2(E2), .E1(E1), .E0(E0), .Branch(Branch), .PCEsc(PCEsc), .IouD(IouD), .EscMem(EscMem),
    .IREsc(IREsc), .MemParaReg(MemParaReg), .RegDst(RegDst), .EscReg(EscReg));
  ULA_PC_Fonte ula_pc_fonte_1 (
    .E3(E3), .E2(E2), .E1(E1), .E0(E0), .UlaFonteA(UlaFonteA), .UlaFonteB1(UlaFonteB1),
    .UlaFonteB0(UlaFonteB0), .PCFonte1(PCFonte1), .PCFonte0(PCFonte0));
  D_Flip_Flop d_ff_1 (.clk(Clock), .D(controle_estados_1_ep3), .Q(E3), .reset(Clear));  // open: Qn, preset, en
  D_Flip_Flop d_ff_2 (.clk(Clock), .D(controle_estados_1_ep2), .Q(E2), .reset(Clear));  // open: Qn, preset, en
  D_Flip_Flop d_ff_3 (.clk(Clock), .D(controle_estados_1_ep1), .Q(E1), .reset(Clear));  // open: Qn, preset, en
  D_Flip_Flop d_ff_4 (.clk(Clock), .D(controle_estados_1_ep0), .Q(E0), .reset(Clear));  // open: Qn, preset, en

  // Other names for the same wires on the sheet: Clk = Clock
endmodule
